# Fritzing sketch Initial_prototype_layout_early (saved by Fritzing 0.9.5d)
breadboards: 1

parts:
  Part1 = Arduino Pro Mini (3.3V)
  Part2 = GY-GPS6MV2
  Part3 = Adafruit PCF8574 [part_number="Adafruit #5545"]
  hc-sr1 = hc-sr04
  U1 = LoRaWAN RN2483/RN2903 Breakout board
  S1 = Pushbutton [package="[SMD]"]
  10k = Resistor [tolerance=±5% resistance=220 package=THT]
  J1 = Piezo Speaker
  R1 = PHOTOCELL [package=photocell-kit]
  10k_2 = Resistor [tolerance=±5% resistance=220 package=THT]
  LED1 = LED - 5mm [color="Red (633nm)" package="5 mm [THT]"]
  R2 = Resistor [tolerance=±5% resistance=220 package=THT]
  VCC1 = Battery
  10k_3 = Resistor [tolerance=±5% resistance=220 package=THT]
  10k_4 = Resistor [tolerance=±5% resistance=220 package=THT]

nets:
  N1: Part1.A4, Part3.SDA
  N2: Part1.A5, Part3.SCL
  VCC: Part1.VCC, Part2.VCC, Part3.VCC, hc-sr1.VCC, U1.3V3, S1.Pin_3, S1.Pin_4, R1.P$2
  GND: Part2.GND, Part3.GND, hc-sr1.GND, U1.GND, 10k.Pin_1, J1.pin1, 10k_2.Pin_0, LED1.cathode, VCC1.-, 10k_4.Pin_1
  N3: S1.Pin_1, S1.Pin_2, 10k.Pin_0
  N4: R1.P$1, 10k_2.Pin_1
  N5: LED1.anode, R2.Pin_1
  N6: VCC1.+, 10k_3.Pin_1
  N7: 10k_3.Pin_0, 10k_4.Pin_0

custom parts:
  GY-GPS6MV2: Based on u-blox NEO-6M GPS Breakout credit for niccolo@rigacci.org
  Adafruit PCF8574: Expand your project possibilities, with the Adafruit PCF8574 GPIO Expander Breakout - an affordable 8 channel I2C expander. GPIO expanders work like this: you have a board with some number of GPIO but not enough for your project - maybe you need more buttons or LEDs. You could upgrade to a board with massive number of GPIO like the Grand Central, or you could pop on one of these boards.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
  LoRaWAN RN2483/RN2903 Breakout board: This breakout board offers an affordable solution for makers working with the popular RN2483A and RN2903A LoRa transceivers from Microchip, widely used for LoRaWAN (Commonly called just RN2483 and RN2903, or collectively, RN2xx3). The layout of this breakout board is based on the the datasheet reference designs. This board breaks out all 14 GPIO pins to a row of 0.1" pin header, and the power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
